# Fritzing sketch circuit (saved by Fritzing 0.9.4)
breadboards: 2

parts:
  Part1 = Arduino Nano (Rev3.0)
  Pololu_A1 = Pololu A4988 [package=SO16]
  Pololu_A2 = Pololu A4988 [package=SO16]
  Pololu_A3 = Pololu A4988 [package=SO16]
  Pololu_A4 = Pololu A4988 [package=SO16]
  Power_plug1 = Power plug
  Pololu_A5 = Pololu A4988 [package=SO16]

nets:
  N1: Part1.GND, Pololu_A1.GND#8, Pololu_A2.GND#8, Pololu_A3.GND#8, Pololu_A4.GND#8, Pololu_A5.GND#8
  N2: Part1.D2, Pololu_A1.DIR, Pololu_A2.DIR, Pololu_A3.DIR, Pololu_A4.DIR, Pololu_A5.DIR
  N3: Part1.D3, Pololu_A1.STEP
  N4: Part1.D4, Pololu_A2.STEP
  N5: Part1.D5, Pololu_A3.STEP
  N6: Part1.D6, Pololu_A4.STEP
  N7: Part1.D7, Pololu_A5.STEP
  VDD: Part1.5V, Pololu_A1.VDD, Pololu_A2.VDD, Pololu_A3.VDD, Pololu_A4.VDD, Pololu_A5.VDD
  N8: Pololu_A1.RESET, Pololu_A1.SLEEP
  N9: Pololu_A1.GND#14, Pololu_A2.GND#14, Pololu_A3.GND#14, Pololu_A4.GND#14, Power_plug1.GND, Pololu_A5.GND#14
  N10: Pololu_A1.VMOT, Pololu_A2.VMOT, Pololu_A3.VMOT, Pololu_A4.VMOT, Power_plug1.VCC, Pololu_A5.VMOT
  N11: Pololu_A2.RESET, Pololu_A2.SLEEP
  N12: Pololu_A3.RESET, Pololu_A3.SLEEP
  N13: Pololu_A4.RESET, Pololu_A4.SLEEP
  N14: Pololu_A5.RESET, Pololu_A5.SLEEP
